// Digital circuit hardware.dig as structural Verilog
module hardware (
  input  clk,
  input  in_2,
  input  [3:0] in_3,
  input  [3:0] in_4,
  input  [3:0] in_5,
  input  [3:0] in_6,
  input  [15:0] in_7,
  input  in_8,
  input  [15:0] in_9,
  input  in_10,
  input  in_11,
  input  in_12,
  input  [15:0] in_13,
  input  in_14,
  input  [15:0] in_15,
  input  in_16,
  input  in_17,
  input  [15:0] in_18
);

  wire alu_1_fn, PC_ovf;
  wire [15:0] InstrReg_q, PC_out, ramdualport_1_d, registerfile_1_da, registerfile_1_db;

  Register #(.Bits(16)) InstrReg (.D(in_7), .C(clk), .en(in_8), .Q(InstrReg_q));
  // Probe on InstrReg_q
  RegisterFile #(.AddrBits(4), .Bits(16)) registerfile_1 (
    .Din(in_9), .we(in_2), .Rw(in_3), .C(clk), .Ra(in_4), .Rb(in_5), .Da(registerfile_1_da),
    .Db(registerfile_1_db));
  CounterPreset #(.Bits(16)) PC (
    .en(in_10), .C(clk), .dir(in_11), .in(in_13), .ld(in_12), .clr(in_14), .out(PC_out), .ovf(PC_ovf));
  // Probe on PC_out
  // Probe on PC_ovf
  alu alu_1 (.Op(in_6), .TData(registerfile_1_da), .AData(registerfile_1_db), .fN(alu_1_fn));  // open: RData, fZ
  RAMDualPort #(.AddrBits(16), .Bits(16)) ramdualport_1 (
    .A(in_15), .Din(in_18), .str(in_16), .C(clk), .ld(in_17), .D(ramdualport_1_d));
  // Probe on alu_1_fn
  // Probe on ramdualport_1_d
endmodule
